# Fritzing sketch ASTA (saved by Fritzing 0.9.3b)
breadboards: 1

parts:
  Part1 = Arduino Uno (Rev3)
  U2 = LCD-16X2 [package=lcd-16x2_noholes]
  R1 = Trimmer Potentiometer [maximum_resistance=10kΩ package=THT]
  SP1 = SPEAKER [package=pcb_mount_speaker]
  S1 = Pushbutton [package="[THT]"]
  LED1 = LED - 5mm [color="White (4500K)" package="5 mm [THT]"]
  R2 = Resistor [tolerance=±5% resistance=100k package=THT]
  Part3 = Bluetooth HC-05 Macho

nets:
  N1: Part1.A0, S1.Pin_3, S1.Pin_4, R2.Pin_1
  N2: Part1.D8, U2.DB4
  N3: Part1.D9_PWM, U2.E
  N4: Part1.D11_PWM/MOSI, SP1.+, SP1.-, LED1.anode
  N5: Part1.D2, Part3.TXD
  N6: Part1.D3_PWM, Part3.RXD
  N7: Part1.D4, U2.DB7
  N8: Part1.D5_PWM, U2.DB6
  N9: Part1.D6_PWM, U2.DB5
  N10: Part1.D7, U2.RS
  5V: Part1.5V, U2.VDD, U2.A, S1.Pin_1, S1.Pin_2, Part3.VCC
  GND: Part1.GND, U2.VSS, U2.R_W, U2.K, LED1.cathode, R2.Pin_0, Part3.GND
  N11: U2.VO, R1.wiper
